# Fritzing sketch fight-vest-scatch (saved by Fritzing 0.9.3b)

parts:
  Part1 = Arduino Uno (Rev3)
  Part2 = Bluetooth HC-05 Macho
  Part3 = Arduino Pro Mini (5V)
  R2 = Resistor [tolerance=±5% resistance=220 package="0603 [SMD]"]
  R3 = Resistor [tolerance=±5% resistance=220 package="0603 [SMD]"]  # not connected
  U2 = MIC [package=mic-9.7mm]
  U4 = MIC [package=mic-9.7mm]
  R4 = Resistor [tolerance=±5% resistance=220 package="0603 [SMD]"]
  U5 = MIC [package=mic-9.7mm]
  U6 = MIC [package=mic-9.7mm]

nets:
  N1: Part1.D0/RX, Part2.TXD, Part3.RXI
  N2: Part1.D1/TX, Part3.TXO, R4.Pin_1
  N3: Part1.RESET, Part3.RESET
  5V: Part1.5V, Part3.VCC
  GND: Part1.GND, Part2.GND, Part3.GND
  N4: Part2.RXD, R2.Pin_1, R4.Pin_0
  N5: Part3.A0, U2.2
  N6: U2.1, U4.2
  N7: U5.1, U6.2
